// Logisim project project.circ as structural Verilog: 1 circuit, main circuit main
module main (
);

  wire adder_1_cout, and_2_out, and_3_out, and_4_out, and_5_out, and_6_out, and_7_out, and_8_out, and_9_out,
       and_10_out, and_11_out, and_12_out, and_13_out, and_14_out, and_15_out, and_16_out, and_17_out,
       and_18_out, and_19_out, clock_1_out, comparator_1_eq, comparator_2_eq, comparator_3_eq,
       comparator_4_eq, comparator_5_eq, comparator_6_eq, comparator_6_lt, comparator_7_eq, comparator_8_eq,
       comparator_8_gt, comparator_9_eq, comparator_11_eq, comparator_13_eq, comparator_15_eq,
       comparator_16_eq, comparator_17_eq, comparator_18_eq, comparator_19_eq, comparator_20_eq,
       comparator_21_eq, comparator_22_eq, comparator_23_eq, comparator_24_eq, comparator_25_eq,
       comparator_26_eq, comparator_27_eq, comparator_28_eq, comparator_29_eq, comparator_30_eq,
       comparator_31_eq, comparator_32_eq, comparator_33_eq, comparator_34_eq, comparator_35_eq,
       comparator_36_eq, comparator_37_eq, comparator_38_eq, comparator_39_eq, comparator_40_eq,
       comparator_41_eq, pc_carry, pull_resistor_1_node, pull_resistor_2_node, pull_resistor_3_node,
       pull_resistor_4_node, pull_resistor_6_node, pull_resistor_7_node, pull_resistor_8_node, RESET_out,
       STEP_out, subtractor_1_bout;
  wire [1:0] counter_1_q;
  wire [3:0] REG_A_q, REG_A_q_2;
  wire [7:0] adder_1_out, and_1_out, controlled_buffer_1_out, controlled_buffer_12_out,
       controlled_buffer_13_out, not_1_out, or_1_out, pc_q, pc_q_2, prog_data, subtractor_1_out, xor_1_out;
  wire [7:7] comparator_10_lt, comparator_12_gt, comparator_14_eq, or_2_out, or_3_out, REG_CARRY_q;
  wire [15:0] controlled_buffer_17_out, REG_B_q;

  Clock clock_1 (.out(clock_1_out));
  Pull_Resistor pull_resistor_1 (.node(pull_resistor_1_node));
  buf buffer_1 (pull_resistor_1_node, clock_1_out);
  buf buffer_2 (pull_resistor_1_node, STEP_out);
  Counter #(.max('h3), .width(2)) counter_1 (
    .clr(RESET_out), .clk(pull_resistor_1_node), .D(2'b00), .Q(counter_1_q));  // open: load, up, count, carry
  Button RESET (.out(RESET_out));
  Pull_Resistor pull_resistor_2 (.node(pull_resistor_2_node));
  buf buffer_3 (pull_resistor_2_node, comparator_1_eq);
  Comparator #(.width(2)) comparator_1 (.a(2'b00), .b(counter_1_q), .eq(comparator_1_eq));  // open: gt, lt
  Counter #(.max('hffff), .width(16)) pc (
    .clr(RESET_out), .load(pull_resistor_8_node), .clk(pull_resistor_2_node), .D(controlled_buffer_17_out),
    .carry(pc_carry), .Q({pc_q_2, pc_q}));  // open: up, count
  buf buffer_4 (pull_resistor_2_node, pull_resistor_8_node);
  LED overflow (.in(pc_carry));
  Button STEP (.out(STEP_out));
  ROM #(.addrWidth(16)) prog (.addr({pc_q_2, pc_q}), .data(prog_data));
  Hex_Digit_Display hex_digit_display_1 (.value(REG_A_q_2));  // open: dp
  Hex_Digit_Display hex_digit_display_2 (.value(REG_B_q[7:4]));  // open: dp
  Hex_Digit_Display hex_digit_display_3 (.value(REG_B_q[15:12]));  // open: dp
  Hex_Digit_Display hex_digit_display_4 (.value(REG_A_q));  // open: dp
  Hex_Digit_Display hex_digit_display_5 (.value(REG_B_q[3:0]));  // open: dp
  Hex_Digit_Display hex_digit_display_6 (.value(REG_B_q[11:8]));  // open: dp
  Register REG_A (
    .D(controlled_buffer_1_out), .clk(pull_resistor_3_node), .Q({REG_A_q_2, REG_A_q}), .clr(RESET_out));  // open: en
  LED led_1 (.in(pull_resistor_3_node));
  Register REG_B (
    .D(controlled_buffer_12_out), .clk(pull_resistor_4_node), .Q(REG_B_q[7:0]), .clr(RESET_out));  // open: en
  LED led_2 (.in(pull_resistor_4_node));
  Register REG_C (
    .D(controlled_buffer_13_out), .clk(pull_resistor_4_node), .Q(REG_B_q[15:8]), .clr(RESET_out));  // open: en
  LED led_3 (.in(pull_resistor_4_node));
  Register #(.width(1)) REG_CARRY (
    .D(pull_resistor_6_node), .clk(pull_resistor_7_node), .Q(REG_CARRY_q[7]), .clr(RESET_out));  // open: en
  LED led_4 (.in(pull_resistor_7_node));
  Pull_Resistor pull_resistor_3 (.node(pull_resistor_3_node));
  Pull_Resistor pull_resistor_4 (.node(pull_resistor_4_node));
  Pull_Resistor pull_resistor_5 (.node(pull_resistor_4_node));
  Pull_Resistor pull_resistor_6 (.node(pull_resistor_6_node));
  Pull_Resistor pull_resistor_7 (.node(pull_resistor_7_node));
  Pull_Resistor pull_resistor_8 (.node(pull_resistor_8_node));
  assign controlled_buffer_1_out = comparator_3_eq ? adder_1_out : 8'bz;  // Controlled_Buffer controlled_buffer_1
  buf buffer_5 (pull_resistor_3_node, and_4_out);
  buf buffer_6 (pull_resistor_7_node, and_4_out);
  assign controlled_buffer_1_out = comparator_4_eq ? subtractor_1_out : 8'bz;  // Controlled_Buffer controlled_buffer_2
  buf buffer_7 (pull_resistor_3_node, and_5_out);
  buf buffer_8 (pull_resistor_7_node, and_5_out);
  assign controlled_buffer_1_out = comparator_5_eq ? {8{or_2_out[7]}} : 8'bz;  // Controlled_Buffer controlled_buffer_3
  assign controlled_buffer_1_out = comparator_7_eq ? {8{or_3_out[7]}} : 8'bz;  // Controlled_Buffer controlled_buffer_4
  assign controlled_buffer_1_out = comparator_9_eq ? {8{comparator_10_lt[7]}} : 8'bz;  // Controlled_Buffer controlled_buffer_5
  assign controlled_buffer_1_out = comparator_11_eq ? {8{comparator_12_gt[7]}} : 8'bz;  // Controlled_Buffer controlled_buffer_6
  assign controlled_buffer_1_out = comparator_13_eq ? {8{comparator_14_eq[7]}} : 8'bz;  // Controlled_Buffer controlled_buffer_7
  assign controlled_buffer_1_out = comparator_15_eq ? and_1_out : 8'bz;  // Controlled_Buffer controlled_buffer_8
  assign controlled_buffer_1_out = comparator_16_eq ? or_1_out : 8'bz;  // Controlled_Buffer controlled_buffer_9
  assign controlled_buffer_1_out = comparator_17_eq ? xor_1_out : 8'bz;  // Controlled_Buffer controlled_buffer_10
  assign controlled_buffer_1_out = comparator_18_eq ? not_1_out : 8'bz;  // Controlled_Buffer controlled_buffer_11
  assign controlled_buffer_12_out = comparator_19_eq ? pc_q : 8'bz;  // Controlled_Buffer controlled_buffer_12
  assign controlled_buffer_13_out = comparator_19_eq ? pc_q_2 : 8'bz;  // Controlled_Buffer controlled_buffer_13
  assign controlled_buffer_1_out = comparator_20_eq ? {8{REG_CARRY_q[7]}} : 8'bz;  // Controlled_Buffer controlled_buffer_14
  Comparator comparator_2 (.a(prog_data), .b({8{1'b0}}), .eq(comparator_2_eq));  // open: gt, lt
  LED NOOP (.in(comparator_2_eq));
  Comparator comparator_3 (.a(prog_data), .b(8'h1), .eq(comparator_3_eq));  // open: gt, lt
  LED ADD (.in(comparator_3_eq));
  assign pull_resistor_6_node = comparator_3_eq ? adder_1_cout : 1'bz;  // Controlled_Buffer controlled_buffer_15
  Comparator comparator_4 (.a(prog_data), .b(8'h2), .eq(comparator_4_eq));  // open: gt, lt
  LED SUB (.in(comparator_4_eq));
  assign pull_resistor_6_node = comparator_4_eq ? subtractor_1_bout : 1'bz;  // Controlled_Buffer controlled_buffer_16
  Comparator comparator_5 (.a(prog_data), .b(8'h10), .eq(comparator_5_eq));  // open: gt, lt
  LED LTEQ (.in(comparator_5_eq));
  Comparator #(.mode("unsigned")) comparator_6 (
    .a({REG_A_q_2, REG_A_q}), .b(REG_B_q[7:0]), .eq(comparator_6_eq), .lt(comparator_6_lt));  // open: gt
  Comparator comparator_7 (.a(prog_data), .b(8'h11), .eq(comparator_7_eq));  // open: gt, lt
  LED GTEQ (.in(comparator_7_eq));
  Comparator #(.mode("unsigned")) comparator_8 (
    .a({REG_A_q_2, REG_A_q}), .b(REG_B_q[7:0]), .gt(comparator_8_gt), .eq(comparator_8_eq));  // open: lt
  Comparator comparator_9 (.a(prog_data), .b(8'h12), .eq(comparator_9_eq));  // open: gt, lt
  LED LT (.in(comparator_9_eq));
  Comparator #(.mode("unsigned")) comparator_10 (
    .a({REG_A_q_2, REG_A_q}), .b(REG_B_q[7:0]), .lt(comparator_10_lt[7]));  // open: gt, eq
  Comparator comparator_11 (.a(prog_data), .b(8'h13), .eq(comparator_11_eq));  // open: gt, lt
  LED GT (.in(comparator_11_eq));
  Comparator #(.mode("unsigned")) comparator_12 (
    .a({REG_A_q_2, REG_A_q}), .b(REG_B_q[7:0]), .gt(comparator_12_gt[7]));  // open: eq, lt
  Comparator comparator_13 (.a(prog_data), .b(8'h14), .eq(comparator_13_eq));  // open: gt, lt
  LED EQ (.in(comparator_13_eq));
  Comparator #(.mode("unsigned")) comparator_14 (
    .a({REG_A_q_2, REG_A_q}), .b(REG_B_q[7:0]), .eq(comparator_14_eq[7]));  // open: gt, lt
  Comparator comparator_15 (.a(prog_data), .b(8'h20), .eq(comparator_15_eq));  // open: gt, lt
  LED AND_BITWISE (.in(comparator_15_eq));
  assign and_1_out = {REG_A_q_2, REG_A_q} & REG_B_q[7:0];  // AND_Gate and_1, 8 bits wide
  Comparator comparator_16 (.a(prog_data), .b(8'h21), .eq(comparator_16_eq));  // open: gt, lt
  LED OR_BITWISE (.in(comparator_16_eq));
  assign or_1_out = {REG_A_q_2, REG_A_q} | REG_B_q[7:0];  // OR_Gate or_1, 8 bits wide
  Comparator comparator_17 (.a(prog_data), .b(8'h22), .eq(comparator_17_eq));  // open: gt, lt
  LED XOR_BITWISE (.in(comparator_17_eq));
  assign xor_1_out = {REG_A_q_2, REG_A_q} ^ REG_B_q[7:0];  // XOR_Gate xor_1, 8 bits wide
  Comparator comparator_18 (.a(prog_data), .b(8'h23), .eq(comparator_18_eq));  // open: gt, lt
  LED NOT_BITWISE (.in(comparator_18_eq));
  assign not_1_out = ~{REG_A_q_2, REG_A_q};  // NOT_Gate not_1, 8 bits wide
  Comparator comparator_19 (.a(prog_data), .b(8'h30), .eq(comparator_19_eq));  // open: gt, lt
  LED GET_PC (.in(comparator_19_eq));
  Comparator comparator_20 (.a(prog_data), .b(8'h31), .eq(comparator_20_eq));  // open: gt, lt
  LED GET_CARRY (.in(comparator_20_eq));
  Comparator comparator_21 (.a(prog_data), .b(8'h40), .eq(comparator_21_eq));  // open: gt, lt
  LED JUMP (.in(comparator_21_eq));
  buf buffer_9 (pull_resistor_8_node, and_17_out);
  assign controlled_buffer_17_out = and_17_out ? REG_B_q : 16'bz;  // Controlled_Buffer controlled_buffer_17
  Comparator comparator_22 (.a(prog_data), .b(8'h41), .eq(comparator_22_eq));  // open: gt, lt
  LED JUMPI (.in(comparator_22_eq));
  buf buffer_10 (pull_resistor_8_node, and_2_out);
  and and_2 (and_2_out, and_18_out, comparator_23_eq);
  assign controlled_buffer_17_out = and_2_out ? REG_B_q : 16'bz;  // Controlled_Buffer controlled_buffer_18
  Comparator comparator_23 (.a({REG_A_q_2, REG_A_q}), .b({8{1'b1}}), .eq(comparator_23_eq));  // open: gt, lt
  Comparator comparator_24 (.a(prog_data), .b(8'h42), .eq(comparator_24_eq));  // open: gt, lt
  LED JUMPZ (.in(comparator_24_eq));
  buf buffer_11 (pull_resistor_8_node, and_3_out);
  and and_3 (and_3_out, and_19_out, comparator_25_eq);
  assign controlled_buffer_17_out = and_3_out ? REG_B_q : 16'bz;  // Controlled_Buffer controlled_buffer_19
  Comparator comparator_25 (.a({REG_A_q_2, REG_A_q}), .b({8{1'b0}}), .eq(comparator_25_eq));  // open: gt, lt
  Comparator #(.width(2)) comparator_26 (.a(2'b01), .b(counter_1_q), .eq(comparator_26_eq));  // open: gt, lt
  and and_4 (and_4_out, comparator_26_eq, comparator_3_eq);
  Adder adder_1 (.a({REG_A_q_2, REG_A_q}), .b(REG_B_q[7:0]), .out(adder_1_out), .cout(adder_1_cout));  // open: cin
  Comparator #(.width(2)) comparator_27 (.a(2'b01), .b(counter_1_q), .eq(comparator_27_eq));  // open: gt, lt
  and and_5 (and_5_out, comparator_27_eq, comparator_4_eq);
  Subtractor subtractor_1 (
    .a({REG_A_q_2, REG_A_q}), .b(REG_B_q[7:0]), .out(subtractor_1_out), .bout(subtractor_1_bout));  // open: bin
  Comparator #(.width(2)) comparator_28 (.a(2'b01), .b(counter_1_q), .eq(comparator_28_eq));  // open: gt, lt
  or or_2 (or_2_out[7], comparator_6_eq, comparator_6_lt);
  and and_6 (and_6_out, comparator_28_eq, comparator_5_eq);
  buf buffer_12 (pull_resistor_3_node, and_6_out);
  Comparator #(.width(2)) comparator_29 (.a(2'b01), .b(counter_1_q), .eq(comparator_29_eq));  // open: gt, lt
  or or_3 (or_3_out[7], comparator_8_gt, comparator_8_eq);
  and and_7 (and_7_out, comparator_29_eq, comparator_7_eq);
  buf buffer_13 (pull_resistor_3_node, and_7_out);
  Comparator #(.width(2)) comparator_30 (.a(2'b01), .b(counter_1_q), .eq(comparator_30_eq));  // open: gt, lt
  and and_8 (and_8_out, comparator_30_eq, comparator_9_eq);
  buf buffer_14 (pull_resistor_3_node, and_8_out);
  Comparator #(.width(2)) comparator_31 (.a(2'b01), .b(counter_1_q), .eq(comparator_31_eq));  // open: gt, lt
  and and_9 (and_9_out, comparator_31_eq, comparator_11_eq);
  buf buffer_15 (pull_resistor_3_node, and_9_out);
  Comparator #(.width(2)) comparator_32 (.a(2'b01), .b(counter_1_q), .eq(comparator_32_eq));  // open: gt, lt
  and and_10 (and_10_out, comparator_32_eq, comparator_13_eq);
  buf buffer_16 (pull_resistor_3_node, and_10_out);
  Comparator #(.width(2)) comparator_33 (.a(2'b01), .b(counter_1_q), .eq(comparator_33_eq));  // open: gt, lt
  and and_11 (and_11_out, comparator_33_eq, comparator_15_eq);
  buf buffer_17 (pull_resistor_3_node, and_11_out);
  Comparator #(.width(2)) comparator_34 (.a(2'b01), .b(counter_1_q), .eq(comparator_34_eq));  // open: gt, lt
  and and_12 (and_12_out, comparator_34_eq, comparator_16_eq);
  buf buffer_18 (pull_resistor_3_node, and_12_out);
  Comparator #(.width(2)) comparator_35 (.a(2'b01), .b(counter_1_q), .eq(comparator_35_eq));  // open: gt, lt
  and and_13 (and_13_out, comparator_35_eq, comparator_17_eq);
  buf buffer_19 (pull_resistor_3_node, and_13_out);
  Comparator #(.width(2)) comparator_36 (.a(2'b01), .b(counter_1_q), .eq(comparator_36_eq));  // open: gt, lt
  and and_14 (and_14_out, comparator_36_eq, comparator_18_eq);
  buf buffer_20 (pull_resistor_3_node, and_14_out);
  Comparator #(.width(2)) comparator_37 (.a(2'b01), .b(counter_1_q), .eq(comparator_37_eq));  // open: gt, lt
  and and_15 (and_15_out, comparator_37_eq, comparator_19_eq);
  buf buffer_21 (pull_resistor_4_node, and_15_out);
  Comparator #(.width(2)) comparator_38 (.a(2'b01), .b(counter_1_q), .eq(comparator_38_eq));  // open: gt, lt
  and and_16 (and_16_out, comparator_38_eq, comparator_20_eq);
  buf buffer_22 (pull_resistor_3_node, and_16_out);
  Comparator #(.width(2)) comparator_39 (.a(2'b11), .b(counter_1_q), .eq(comparator_39_eq));  // open: gt, lt
  and and_17 (and_17_out, comparator_39_eq, comparator_21_eq);
  Comparator #(.width(2)) comparator_40 (.a(2'b11), .b(counter_1_q), .eq(comparator_40_eq));  // open: gt, lt
  and and_18 (and_18_out, comparator_40_eq, comparator_22_eq);
  Comparator #(.width(2)) comparator_41 (.a(2'b11), .b(counter_1_q), .eq(comparator_41_eq));  // open: gt, lt
  and and_19 (and_19_out, comparator_41_eq, comparator_24_eq);

  // Notes on the sheet:
  //   buffer_1 drives only 1 and floats otherwise
  //   buffer_2 drives only 1 and floats otherwise
  //   buffer_3 drives only 1 and floats otherwise
  //   buffer_4 drives only 1 and floats otherwise
  //   contents of prog (hex, n*v repeats v):
  //   1 1 14 42 4*2 88*1
  //   buffer_5 drives only 1 and floats otherwise
  //   buffer_6 drives only 1 and floats otherwise
  //   buffer_7 drives only 1 and floats otherwise
  //   buffer_8 drives only 1 and floats otherwise
  //   buffer_9 drives only 1 and floats otherwise
  //   buffer_10 drives only 1 and floats otherwise
  //   buffer_11 drives only 1 and floats otherwise
  //   buffer_12 drives only 1 and floats otherwise
  //   buffer_13 drives only 1 and floats otherwise
  //   buffer_14 drives only 1 and floats otherwise
  //   buffer_15 drives only 1 and floats otherwise
  //   buffer_16 drives only 1 and floats otherwise
  //   buffer_17 drives only 1 and floats otherwise
  //   buffer_18 drives only 1 and floats otherwise
  //   buffer_19 drives only 1 and floats otherwise
  //   buffer_20 drives only 1 and floats otherwise
  //   buffer_21 drives only 1 and floats otherwise
  //   buffer_22 drives only 1 and floats otherwise
endmodule
